// Logisim project CPU.circ as structural Verilog: 4 circuits, main circuit main
module main (
);

  wire button_1_out, button_2_out, program_logic_1_reg1_read_en, program_logic_1_reg1_write_en;
  wire [1:0] program_logic_1_reg1_sel;
  wire [3:0] program_logic_1_output1, register_bank_1_reg1_output, register_bank_1_reg2_output;

  Button button_1 (.out(button_1_out));
  Button button_2 (.out(button_2_out));
  Program_Logic program_logic_1 (
    .clock(button_1_out), .reset(button_2_out), .Output1(program_logic_1_output1),
    .Reg1_Sel(program_logic_1_reg1_sel), .Reg1_Read_En(program_logic_1_reg1_read_en),
    .Reg1_Write_En(program_logic_1_reg1_write_en));  // open: Output2, Reg2_Sel, Reg2_Read_En, Reg2_Write_En, Compare
  Register_Bank register_bank_1 (
    .reset(button_2_out), .Write_Select(program_logic_1_reg1_sel),
    .Write_Enable(program_logic_1_reg1_write_en), .Input(program_logic_1_output1),
    .Reg1_Output(register_bank_1_reg1_output), .Read_Reg1_En(program_logic_1_reg1_read_en),
    .Read_Reg1_Sel(program_logic_1_reg1_sel), .Reg2_Output(register_bank_1_reg2_output));  // open: Reg_11, Reg_10, Reg_01, Reg_00, Read_Reg2_En, Read_Reg2_Sel
  // Probe on register_bank_1_reg1_output
  // Probe on register_bank_1_reg2_output
  Comparator comparator_1 ();  // open: a, b, gt, eq, lt

  // Notes on the sheet:
  //   Program Logic
  //   Register Bank
endmodule

module Program_Logic (
  input  clock,
  input  reset,
  output [3:0] Output2,
  output [3:0] Output1,
  output [1:0] Reg2_Sel,
  output [1:0] Reg1_Sel,
  output Reg2_Read_En,
  output Reg1_Read_En,
  output Reg2_Write_En,
  output Reg1_Write_En,
  output Compare
);

  wire [7:0] adder_1_out, multiplexer_1_out, multiplexer_2_out, register_1_q, subtractor_1_out;
  wire [18:17] rom_1_data;

  Multiplexer #(.width(8), .enable("false")) multiplexer_1 (
    .in0(8'h1), .in1({4'b0000, Output1}), .out(multiplexer_1_out), .sel(rom_1_data[18]));
  Adder adder_1 (.a(multiplexer_1_out), .b(register_1_q), .out(adder_1_out));  // open: cin, cout
  Multiplexer #(.width(8), .enable("false")) multiplexer_2 (
    .in0(adder_1_out), .in1(subtractor_1_out), .out(multiplexer_2_out), .sel(rom_1_data[17]));
  Subtractor subtractor_1 (.a(multiplexer_1_out), .b(register_1_q), .out(subtractor_1_out));  // open: bin, bout
  // Probe on multiplexer_2_out
  Register register_1 (.D(multiplexer_2_out), .Q(register_1_q), .clk(clock), .clr(reset));  // open: en
  ROM #(.dataWidth(19)) rom_1 (
    .addr(register_1_q),
    .data({rom_1_data, Compare, Reg1_Write_En, Reg2_Write_En, Reg1_Read_En, Reg2_Read_En, Reg1_Sel, Reg2_Sel, Output1, Output2}));  // open: sel

  // Notes on the sheet:
  //   contents of rom_1 (hex, n*v repeats v):
  //   a0a0 a450
endmodule

module Register_Bank (
  input  [1:0] Write_Select,
  input  Write_Enable,
  input  Read_Reg1_En,
  input  [1:0] Read_Reg1_Sel,
  input  Read_Reg2_En,
  input  [3:0] Input,
  input  reset,
  input  [1:0] Read_Reg2_Sel,
  output [3:0] Reg1_Output,
  output [3:0] Reg_11,
  output [3:0] Reg_10,
  output [3:0] Reg_01,
  output [3:0] Reg_00,
  output [3:0] Reg2_Output
);

  wire decoder_1_out0, decoder_1_out1, decoder_1_out2, decoder_1_out3, not_1_out, not_2_out, not_3_out,
       not_4_out;

  Decoder #(.select(2), .disabled(0)) decoder_1 (
    .out0(decoder_1_out0), .out1(decoder_1_out1), .out2(decoder_1_out2), .out3(decoder_1_out3),
    .sel(Write_Select), .en(Write_Enable));
  not not_1 (not_1_out, decoder_1_out3);
  Register #(.width(4), .trigger("high")) register_1 (
    .D(Input), .en(not_1_out), .Q(Reg_11), .clk(decoder_1_out3), .clr(reset));
  Register #(.width(4), .trigger("high")) register_2 (
    .D(Input), .en(not_2_out), .Q(Reg_10), .clk(decoder_1_out2), .clr(reset));
  not not_2 (not_2_out, decoder_1_out2);
  not not_3 (not_3_out, decoder_1_out1);
  Register #(.width(4), .trigger("high")) register_3 (
    .D(Input), .en(not_3_out), .Q(Reg_01), .clk(decoder_1_out1), .clr(reset));
  Register #(.width(4), .trigger("high")) register_4 (
    .D(Input), .en(not_4_out), .Q(Reg_00), .clk(decoder_1_out0), .clr(reset));
  not not_4 (not_4_out, decoder_1_out0);
  Multiplexer #(.select(2), .width(4)) multiplexer_1 (
    .in0(Reg_00), .in1(Reg_01), .in2(Reg_10), .in3(Reg_11), .out(Reg1_Output), .sel(Read_Reg1_Sel),
    .en(Read_Reg1_En));
  Multiplexer #(.select(2), .width(4)) multiplexer_2 (
    .in0(Reg_00), .in1(Reg_01), .in2(Reg_10), .in3(Reg_11), .out(Reg2_Output), .sel(Read_Reg2_Sel),
    .en(Read_Reg2_En));
endmodule

module Arithmics (
  input  [3:0] Input_1,
  input  [3:0] Input_2,
  input  Enable,
  input  [1:0] Function_Select,
  output [3:0] Output
);

  wire [3:0] adder_1_out, divider_1_out, multiplier_1_out, subtractor_1_out;

  Adder #(.width(4)) adder_1 (.a(Input_1), .b(Input_2), .out(adder_1_out));  // open: cin, cout
  Subtractor #(.width(4)) subtractor_1 (.a(Input_1), .b(Input_2), .out(subtractor_1_out));  // open: bin, bout
  Multiplier #(.width(4)) multiplier_1 (.a(Input_1), .b(Input_2), .out(multiplier_1_out));  // open: cin, cout
  Divider #(.width(4)) divider_1 (.a(Input_1), .b(Input_2), .out(divider_1_out));  // open: upper, rem
  Multiplexer #(.select(2), .width(4)) multiplexer_1 (
    .in0(adder_1_out), .in1(subtractor_1_out), .in2(multiplier_1_out), .in3(divider_1_out), .out(Output),
    .sel(Function_Select), .en(Enable));
endmodule
